# Fritzing sketch CowPi-mk1i-pico-nowires (saved by Fritzing 1.0.0rc)
breadboards: 1

parts:
  S9 = Pushbutton [package="[THT]"]
  S10 = Toggle Switch [package=THT]  # not connected
  S11 = Toggle Switch [package=THT]  # not connected
  Keypad4x2 = Keypad Membran 4x4  # not connected
  S12 = Pushbutton [package="[THT]"]
  Mod1 = Raspberry Pi Pico
  S13 = Momentary Switch 6mm 2pin
  S14 = Momentary Switch 6mm 2pin
  R1 = Resistor [tolerance=±5% resistance=560 package="0603 [SMD]"]
  LED1 = LED - 5mm [color="Red (633nm)" current=0.030A package="5 mm [THT]"]
  LED2 = LED - 5mm [color="Green (555nm)" current=0.030A package="5 mm [THT]"]
  OLED1 = OLED 128x64 I2C Monochrome Display  # not connected
  R2 = Resistor [tolerance=±5% power=0.25W resistance=560 package=THT]

nets:
  N1: S9.Pin_1, S9.Pin_2
  N2: S9.Pin_3, S9.Pin_4
  N3: S12.Pin_1, S12.Pin_2
  N4: S12.Pin_3, S12.Pin_4
  N5: Mod1.pin_3, Mod1.pin_8, Mod1.pin_13, Mod1.pin_18, Mod1.pin_23, Mod1.pin_28, Mod1.pin_33, Mod1.pin_38
  N6: Mod1.pin_4, S13.2
  N7: Mod1.pin_5, S14.1
  N8: Mod1.pin_26, R2.Pin_0
  N9: Mod1.pin_27, R1.Pin_0
  N10: S13.1, S14.2
  N11: R1.Pin_1, LED1.anode
  N12: LED1.cathode, LED2.cathode
  N13: LED2.anode, R2.Pin_1

custom parts:
  Keypad Membran 4x4: Membrane Keypad 4x4 Matrix
  Raspberry Pi Pico: Raspberry Pi Pico. Based around the RP2040 microcontroller the Pico is a low cost microcontroller device bringing Raspberry Pi quality, cost, and easy of use to the microcontroller space. Jan 2021, Split part in to two versions: tht (this one) and SMD. This one will drill holes for a .1 in header in pcb to allow plugging in the module as well as providing pads to solder the module to the top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
  Momentary Switch 6mm 2pin: Momentary Switch 6mm 2 pin Button commonly used for reset or general input.
