# Fritzing sketch CowPi-mk1i-pico-wires (saved by Fritzing 1.0.0rc)
breadboards: 1

parts:
  S9 = Pushbutton [package="[THT]"]
  S10 = Toggle Switch [package=THT]
  S11 = Toggle Switch [package=THT]
  Keypad4x2 = Keypad Membran 4x4
  S12 = Pushbutton [package="[THT]"]
  Mod1 = Raspberry Pi Pico
  R1 = Resistor [tolerance=±5% resistance=560 package="0603 [SMD]"]
  LED1 = LED - 5mm [color="Red (633nm)" current=0.030A package="5 mm [THT]"]
  LED2 = LED - 5mm [color="Green (555nm)" current=0.030A package="5 mm [THT]"]
  OLED1 = OLED 128x64 I2C Monochrome Display
  R2 = Resistor [tolerance=±5% power=0.25W resistance=560 package=THT]

nets:
  N1: S9.Pin_1, S9.Pin_2, S10.COM, S11.COM, S12.Pin_1, S12.Pin_2, Mod1.pin_3, Mod1.pin_8, Mod1.pin_13, Mod1.pin_18, Mod1.pin_23, Mod1.pin_28, Mod1.pin_33, Mod1.pin_38, LED1.cathode, LED2.cathode, OLED1.GND, OLED1.SDA
  N2: S9.Pin_3, S9.Pin_4, Mod1.pin_5
  N3: S10.L1, Mod1.pin_20
  N4: S11.L1, Mod1.pin_19
  N5: Keypad4x2.Pin1, Mod1.pin_9
  N6: Keypad4x2.Pin2, Mod1.pin_10
  N7: Keypad4x2.Pin3, Mod1.pin_11
  N8: Keypad4x2.Pin4, Mod1.pin_12
  N9: Keypad4x2.Pin5, Mod1.pin_14
  N10: Keypad4x2.Pin6, Mod1.pin_15
  N11: Keypad4x2.Pin7, Mod1.pin_16
  N12: Keypad4x2.Pin8, Mod1.pin_17
  N13: S12.Pin_3, S12.Pin_4, Mod1.pin_4
  N14: Mod1.pin_7, OLED1.SCK
  N15: Mod1.pin_26, R2.Pin_0
  N16: Mod1.pin_27, R1.Pin_0
  N17: Mod1.pin_36, OLED1.VDD
  N18: R1.Pin_1, LED1.anode
  N19: LED2.anode, R2.Pin_1

custom parts:
  Keypad Membran 4x4: Membrane Keypad 4x4 Matrix
  Raspberry Pi Pico: Raspberry Pi Pico. Based around the RP2040 microcontroller the Pico is a low cost microcontroller device bringing Raspberry Pi quality, cost, and easy of use to the microcontroller space. Jan 2021, Split part in to two versions: tht (this one) and SMD. This one will drill holes for a .1 in header in pcb to allow plugging in the module as well as providing pads to solder the module to the top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
